# Fritzing sketch digit (saved by Fritzing 0.9.4)
breadboards: 1

parts:
  Pro_Micro = SparkFun Pro Micro
  7_Segment = 7 Segment Display
  R1 = Resistor [tolerance=±5% resistance=330 package="2010 [SMD]"]

nets:
  N1: Pro_Micro.GND, R1.Pin_0
  N2: Pro_Micro.2, 7_Segment.Segment_A#10
  N3: Pro_Micro.3, Pro_Micro.4, 7_Segment.Segment_B
  N4: Pro_Micro.5, 7_Segment.Segment_C
  N5: Pro_Micro.6, 7_Segment.Segment_E
  N6: Pro_Micro.7, 7_Segment.Segment_F
  N7: Pro_Micro.8, 7_Segment.Segment_A#1
  N8: Pro_Micro.9, 7_Segment.Segment_DP
  N9: 7_Segment.common_cathode#8, R1.Pin_1

custom parts:
  SparkFun Pro Micro: The Pro Micro is similar to the Pro Mini except with an ATmega32U4 on board. The USB transceiver inside the 32U4 allows us to add USB connectivity on-board and do away with bulky external USB interface. Based on: https://github.com/unorthodox-engineers/unorthodox-arduino/blob/master/Unorthodox/fritzing/parts/Pro%20Micro.fzpz
